// Logisim project extram_glue_logic.circ as structural Verilog: 1 circuit, main circuit main
module main (
  input  [15:0] ADDR,
  input  [7:0] DATA,
  input  n_WRAM,
  output [18:0] RAM_ADDR,
  output n_OEhi,
  output n_CEhi,
  output n_WEhi,
  output n_OElo,
  output n_CElo,
  output n_WElo
);

  wire ADDR_C2, clock_1_out, n_ADDR_C2, n_ADDR_D, n_ADDR_E, n_SEGD_SEL, n_SEGE_SEL, n_WE, nand_1_out,
       nand_2_out, nand_3_out, nand_6_out, not_1_out, not_4_out, not_5_out;
  wire [7:0] SEGD_q, SEGE_q;

  Clock clock_1 (.out(clock_1_out));
  not not_1 (not_1_out, ADDR[0]);
  nand nand_1 (nand_1_out, ADDR[15], ADDR[14]);
  nand nand_2 (nand_2_out, ~ADDR[13], ADDR[12]);  // NAND_Gate
  nand nand_3 (nand_3_out, ADDR[13], ~ADDR[12]);  // NAND_Gate
  or or_1 (n_WE, clock_1_out, n_WRAM);
  nand nand_4 (n_SEGD_SEL, ADDR_C2, not_1_out);
  nand nand_5 (n_SEGE_SEL, ADDR_C2, ADDR[0]);
  or or_2 (n_ADDR_D, nand_1_out, nand_2_out);
  or or_3 (n_ADDR_E, nand_1_out, nand_3_out);
  nand nand_6 (nand_6_out, n_ADDR_D, n_ADDR_E);
  not not_2 (n_CEhi, nand_6_out);
  or or_4 (n_ADDR_C2, ADDR[8], ~ADDR[9], ADDR[10], ADDR[11], ADDR[12], ADDR[13], ~ADDR[14], ~ADDR[15]);  // OR_Gate
  not not_3 (ADDR_C2, n_ADDR_C2);
  or or_5 (n_WEhi, n_WE, ~n_OElo);  // OR_Gate
  or or_6 (n_WElo, n_WE, n_OElo);
  Register SEGD (.D(DATA), .en(not_4_out), .clk(n_WE), .Q(SEGD_q), .clr(1'b0));
  not not_4 (not_4_out, n_SEGD_SEL);
  Register SEGE (.D(DATA), .en(not_5_out), .clk(n_WE), .Q(SEGE_q), .clr(1'b0));
  not not_5 (not_5_out, n_SEGE_SEL);
  // Probe on SEGD_q
  // Probe on SEGE_q
  not not_6 (n_OEhi, n_OElo);
  Multiplexer #(.width(8)) multiplexer_1 (.in0(SEGD_q), .in1(SEGE_q), .out({n_OElo, RAM_ADDR[18:12]}), .sel(n_ADDR_D));

  assign n_CElo = n_CEhi;
  assign RAM_ADDR[11:0] = ADDR[11:0];

  // Other names for the same wires on the sheet: A12 = ADDR[12]; A13 = ADDR[13]; A14 = ADDR[14]; A15 = ADDR[15];
  //   n_ADDR_DE = n_CEhi; pA19 = n_OElo; pA19_pA12[7:0] = {n_OElo, RAM_ADDR[18:12]}; A0 = ADDR[0];
  //   ADDR_12bit[11:0] = ADDR[11:0]
endmodule
