// Logisim project uart_glue_logic.circ as structural Verilog: 1 circuit, main circuit main
module main (
  input  [15:0] ADDR_BUS,
  input  n_WRAM,
  input  [3:0] SEQ,
  input  CPU_RST,
  input  INTR,
  input  DR,
  input  [7:0] DATA_BUS,
  output n_CSO,
  output [1:0] ADDR,
  output n_RD,
  output n_WR,
  output RST,
  output n_IRQ4,
  output n_IRQ5,
  output [7:0] DATA
);

  wire F26_27_out, nor_1_out, nor_2_out, not_1_out, not_2_out;

  // NoConnect on ADDR_BUS[7:2]
  nand F26_27 (F26_27_out, nor_2_out, nor_1_out);
  nor nor_1 (nor_1_out, ~SEQ[0], SEQ[1], ~SEQ[2], SEQ[3]);  // NOR_Gate
  nor nor_2 (nor_2_out, ~ADDR_BUS[15], ~ADDR_BUS[14], ADDR_BUS[13], ADDR_BUS[12], ADDR_BUS[11], ADDR_BUS[10], ADDR_BUS[9], ~ADDR_BUS[8]);  // NOR_Gate
  not not_1 (not_1_out, F26_27_out);
  not not_2 (not_2_out, n_WRAM);
  // Probe on nor_2_out
  not not_3 (n_CSO, nor_2_out);
  nand F29_30 (n_RD, n_WRAM, not_1_out);
  nand E28_29 (n_WR, not_1_out, not_2_out);
  not not_4 (n_IRQ4, INTR);
  not not_5 (n_IRQ5, DR);

  assign ADDR = ADDR_BUS[1:0];
  assign DATA = DATA_BUS;
  assign RST = CPU_RST;

  // Notes on the sheet:
  //   n_WRAM: initial=0x1
  //   SEQ: initial=0x1
  //   CPU_RST: initial=0x1
  //   DATA_BUS: initial=0xff
  //   ADDR_BUS: initial=0xffff
  //   Group C G-J
  //   and/or data bus stable across sequences 0x4-0x6
  //   Assumes read and write operations that hold the address
endmodule
